// Digital circuit CG-16-1-Processor.dig as structural Verilog
module CG_16_1_Processor (
  input  clk,
  input  in_2,
  input  in_3
);

  wire aawrite, aluwriteflags, and_1_out, and_2_out, and_3_out, and_4_out, and_5_out, aread, awrite, bsread,
       bswrite, carry, carryclear, carryset, ccclr, comparator_1_lt, demultiplexer_1_out_0,
       demultiplexer_1_out_1, disableinterrupts, enableinterrupts, equalclear, equalset, flagsread,
       flagswrite, Gr_RAM_check_eq, irread, irwrite, lessthanclear, lessthanset, mmuread, mmuwrite,
       morethanclear, morethanset, negativeclear, negativeset, or_1_out, Page_Select_q, pcbsclr, pcbsread,
       pcbswrite, pcclr, pcinc, pcread, pcwrite, Program_Counter_ovf, ROM_check_eq, sbread, sbwrite, stread,
       stwrite, xread, xwrite, yread, ywrite, zeroclear, zeroset, zread, zwrite;
  wire [3:0] Control_Counter_out;
  wire [4:0] aluop;
  wire [6:1] Zero_Flag_q;
  wire [7:0] address_bus, Program_Counter_Bank_Select_out;
  wire [11:0] aluflags;
  wire [11:1] busflags;
  wire [15:0] accumulator, address, blockramdualport_1_d, bus, instruction, Program_Counter_out,
       Stack_Base_Pointer_q, Stack_Top_Pointer_q, X_q, Y_q, Z_q;
  wire [50:0] Control_ROM_d, multiplexer_1_out;
  wire [50:32] multiplexer_2_out;

  Register #(.Bits(16)) X (.D(bus), .C(clk), .en(xwrite), .Q(X_q));
  Register #(.Bits(16)) Y (.D(bus), .C(clk), .en(ywrite), .Q(Y_q));
  Register #(.Bits(16)) Z (.D(bus), .C(clk), .en(zwrite), .Q(Z_q));
  Register #(.Bits(16)) u_Accumulator (.D(bus), .C(clk), .en(awrite), .Q(accumulator));
  CounterPreset #(.Bits(16)) Program_Counter (
    .en(pcinc), .C(clk), .dir(1'b0), .in(bus), .ld(pcwrite), .clr(pcclr), .out(Program_Counter_out),
    .ovf(Program_Counter_ovf));
  Register #(.Bits(16)) Instruction_Register (.D(bus), .C(clk), .en(irwrite), .Q(instruction));
  Register #(.Bits(16)) Stack_Top_Pointer (.D(bus), .C(clk), .en(stwrite), .Q(Stack_Top_Pointer_q));
  Register #(.Bits(16)) Stack_Base_Pointer (.D(bus), .C(clk), .en(sbwrite), .Q(Stack_Base_Pointer_q));
  Register #(.Bits(8)) Bank_Select_Register (.D(bus[7:0]), .C(clk), .en(bswrite), .Q(address_bus));
  Register #(.Bits(16)) Address_Access_Register (.D(bus), .C(clk), .en(aawrite), .Q(address));
  assign bus = xread ? X_q : 16'bz;  // Driver driver_1
  assign bus = yread ? Y_q : 16'bz;  // Driver driver_2
  assign bus = zread ? Z_q : 16'bz;  // Driver driver_3
  assign bus = aread ? accumulator : 16'bz;  // Driver driver_4
  assign bus = pcread ? Program_Counter_out : 16'bz;  // Driver driver_5
  CounterPreset #(.Bits(8)) Program_Counter_Bank_Select (
    .en(Program_Counter_ovf), .C(clk), .dir(1'b0), .in(bus[7:0]), .ld(pcbswrite), .clr(pcbsclr),
    .out(Program_Counter_Bank_Select_out));  // open: ovf
  assign bus = irread ? instruction : 16'bz;  // Driver driver_6
  assign bus = stread ? Stack_Top_Pointer_q : 16'bz;  // Driver driver_7
  assign bus = sbread ? Stack_Base_Pointer_q : 16'bz;  // Driver driver_8
  assign bus = bsread ? {{8{1'b0}}, address_bus} : 16'bz;  // Driver driver_9
  assign bus = pcbsread ? {{8{1'b0}}, Program_Counter_Bank_Select_out} : 16'bz;  // Driver driver_10
  Demultiplexer #(.Selector_Bits(8)) demultiplexer_1 (
    .sel(instruction[7:0]), .in(1'b1), .out_0(demultiplexer_1_out_0), .out_1(demultiplexer_1_out_1));  // open: out_2, out_3, out_4, out_5, out_6, out_7, out_8, out_9, out_10, out_11, out_12, out_13, out_14, out_15, out_16, out_17, out_18, out_19, out_20, out_21, out_22, out_23, out_24, out_25, out_26, out_27, out_28, out_29, out_30, out_31, out_32, out_33, out_34, out_35, out_36, out_37, out_38, out_39, out_40, out_41, out_42, out_43, out_44, out_45, out_46, out_47, out_48, out_49, out_50, out_51, out_52, out_53, out_54, out_55, out_56, out_57, out_58, out_59, out_60, out_61, out_62, out_63, out_64, out_65, out_66, out_67, out_68, out_69, out_70, out_71, out_72, out_73, out_74, out_75, out_76, out_77, out_78, out_79, out_80, out_81, out_82, out_83, out_84, out_85, out_86, out_87, out_88, out_89, out_90, out_91, out_92, out_93, out_94, out_95, out_96, out_97, out_98, out_99, out_100, out_101, out_102, out_103, out_104, out_105, out_106, out_107, out_108, out_109, out_110, out_111, out_112, out_113, out_114, out_115, out_116, out_117, out_118, out_119, out_120, out_121, out_122, out_123, out_124, out_125, out_126, out_127, out_128, out_129, out_130, out_131, out_132, out_133, out_134, out_135, out_136, out_137, out_138, out_139, out_140, out_141, out_142, out_143, out_144, out_145, out_146, out_147, out_148, out_149, out_150, out_151, out_152, out_153, out_154, out_155, out_156, out_157, out_158, out_159, out_160, out_161, out_162, out_163, out_164, out_165, out_166, out_167, out_168, out_169, out_170, out_171, out_172, out_173, out_174, out_175, out_176, out_177, out_178, out_179, out_180, out_181, out_182, out_183, out_184, out_185, out_186, out_187, out_188, out_189, out_190, out_191, out_192, out_193, out_194, out_195, out_196, out_197, out_198, out_199, out_200, out_201, out_202, out_203, out_204, out_205, out_206, out_207, out_208, out_209, out_210, out_211, out_212, out_213, out_214, out_215, out_216, out_217, out_218, out_219, out_220, out_221, out_222, out_223, out_224, out_225, out_226, out_227, out_228, out_229, out_230, out_231, out_232, out_233, out_234, out_235, out_236, out_237, out_238, out_239, out_240, out_241, out_242, out_243, out_244, out_245, out_246, out_247, out_248, out_249, out_250, out_251, out_252, out_253, out_254, out_255
  Counter #(.Bits(4)) Control_Counter (.en(~clk), .C(~clk), .clr(ccclr), .out(Control_Counter_out));  // open: ovf
  RS_FF Carry_Flag (.S(carryset), .C(clk), .R(carryclear), .Q(carry));  // open: nQ
  RS_FF Zero_Flag (.S(zeroset), .C(clk), .R(zeroclear), .Q(Zero_Flag_q[1]));  // open: nQ
  RS_FF Negative_Flag (.S(negativeset), .C(clk), .R(negativeclear), .Q(Zero_Flag_q[2]));  // open: nQ
  RS_FF More_Than_Flag (.S(morethanset), .C(clk), .R(morethanclear), .Q(Zero_Flag_q[3]));  // open: nQ
  RS_FF Equal_Flag (.S(equalset), .C(clk), .R(equalclear), .Q(Zero_Flag_q[4]));  // open: nQ
  RS_FF Less_Than_Flag (.S(lessthanset), .C(clk), .R(lessthanclear), .Q(Zero_Flag_q[5]));  // open: nQ
  RS_FF Interrupt_Disable_Flag (.S(disableinterrupts), .C(clk), .R(enableinterrupts), .Q(Zero_Flag_q[6]));  // open: nQ
  LED NOP (.in(demultiplexer_1_out_0));
  LED LDA (.in(demultiplexer_1_out_1));
  assign bus = flagsread ? {{9{1'b0}}, Zero_Flag_q, carry} : 16'bz;  // Driver driver_11
  ROM #(.AddrBits(20), .Bits(51)) Control_ROM (.A({instruction, Control_Counter_out}), .sel(1'b1), .D(Control_ROM_d));
  LED u_Carry (.in(carry));
  LED Zero (.in(Zero_Flag_q[1]));
  LED Negative (.in(Zero_Flag_q[2]));
  LED More_Than (.in(Zero_Flag_q[3]));
  LED Equal (.in(Zero_Flag_q[4]));
  LED Less_Than (.in(Zero_Flag_q[5]));
  LED Interrupt_Disable (.in(Zero_Flag_q[6]));
  Multiplexer #(.Bits(51)) multiplexer_1 (
    .sel(Control_Counter_out[0]), .in_0(51'h2000400), .in_1(51'h40001), .out(multiplexer_1_out));
  Comparator #(.Bits(4)) comparator_1 (.a(Control_Counter_out), .b(4'b0010), .lt(comparator_1_lt));  // open: gt, eq
  Multiplexer #(.Bits(51)) multiplexer_2 (
    .sel(comparator_1_lt), .in_0(Control_ROM_d), .in_1(multiplexer_1_out),
    .out({multiplexer_2_out[50:49], flagswrite, flagsread, ccclr, enableinterrupts, disableinterrupts, multiplexer_2_out[43:32], aluwriteflags, aluop, aawrite, bswrite, bsread, sbwrite, sbread, stwrite, stread, irwrite, irread, pcbsclr, pcbswrite, pcbsread, pcclr, pcinc, pcwrite, pcread, awrite, aread, zwrite, zread, ywrite, yread, xwrite, xread, mmuwrite, mmuread}));
  CG_16_1_ALU cg_16_1_alu_1 (
    .OP(aluop), .A(accumulator), .B(bus), .C_in(carry), .C_out(aluflags[0]), .Z(aluflags[2]),
    .N(aluflags[4]), .A_gt_B(aluflags[6]), .A_eq_B(aluflags[8]), .A_lt_B(aluflags[10]));  // open: X, X_high
  Comparator #(.Bits(8)) Gr_RAM_check (.a(address_bus), .b({8{1'b1}}), .eq(Gr_RAM_check_eq));  // open: gt, lt
  Comparator #(.Bits(8)) ROM_check (.a(address_bus), .b({8{1'b0}}), .eq(ROM_check_eq));  // open: gt, lt
  and and_1 (and_1_out, Gr_RAM_check_eq, mmuread);
  Multiplexer #(.Selector_Bits(2), .Bits(12)) multiplexer_3 (
    .sel({flagswrite, aluwriteflags}), .in_0(multiplexer_2_out[43:32]), .in_1(aluflags),
    .in_2({busflags[11], bus[5], busflags[9], bus[4], busflags[7], bus[3], busflags[5], bus[2], busflags[3], bus[1], busflags[1], bus[0]}),
    .in_3({12{1'b1}}),
    .out({lessthanclear, lessthanset, equalclear, equalset, morethanclear, morethanset, negativeclear, negativeset, zeroclear, zeroset, carryclear, carryset}));
  or or_1 (or_1_out, Gr_RAM_check_eq, ROM_check_eq);
  and and_2 (and_2_out, ROM_check_eq, mmuread);
  and and_3 (and_3_out, ~Gr_RAM_check_eq, mmuwrite);  // And
  and and_4 (and_4_out, mmuwrite, Gr_RAM_check_eq);
  RS_FF Page_Select (.S(in_3), .C(clk), .R(in_2), .Q(Page_Select_q));  // open: nQ
  ROM #(.AddrBits(16), .isProgramMemory("true"), .Bits(16)) rom_1 (.A(address), .sel(and_2_out), .D(bus));
  BlockRAMDualPort #(.AddrBits(24), .Bits(16)) blockramdualport_1 (
    .A({address_bus, address}), .Din(bus), .str(and_3_out), .C(clk), .D(blockramdualport_1_d));
  GraphicCard #(.graphicHeight(160), .graphicWidth(200), .Bits(16)) graphiccard_1 (
    .A(address), .str(and_4_out), .C(clk), .ld(and_1_out), .B(Page_Select_q), .D(bus));
  not not_1 (aluflags[1], aluflags[0]);
  not not_2 (aluflags[3], aluflags[2]);
  not not_3 (aluflags[5], aluflags[4]);
  not not_4 (aluflags[7], aluflags[6]);
  not not_5 (aluflags[9], aluflags[8]);
  not not_6 (aluflags[11], aluflags[10]);
  assign bus = multiplexer_2_out[49] ? {{8{1'b0}}, instruction[7:0]} : 16'bz;  // Driver driver_12
  assign bus = multiplexer_2_out[50] ? {{8{1'b0}}, instruction[15:8]} : 16'bz;  // Driver driver_13
  and and_5 (and_5_out, mmuread, ~or_1_out);  // And
  assign bus = and_5_out ? blockramdualport_1_d : 16'bz;  // Driver driver_14
  not not_7 (busflags[1], bus[0]);
  not not_8 (busflags[3], bus[1]);
  not not_9 (busflags[5], bus[2]);
  not not_10 (busflags[7], bus[3]);
  not not_11 (busflags[9], bus[4]);
  not not_12 (busflags[11], bus[5]);

  // Other names for the same wires on the sheet: busflags (some bits) = bus[5:0]; clock = clk

  // Notes on the sheet:
  //   Registers
  //   Flags
  //   Control Logic
  //   contents of Control_ROM (hex, n*v repeats v):
  //   0,0,400000000000
  //   MMU
  //   ALU
  //   microinstructions
  //   contents of rom_1 (hex, n*v repeats v):
  //   0,1,3,76d3,29*0,1
  //   Bus Flag Decoding
endmodule
